# Fritzing sketch schorlephasediagram (saved by Fritzing 0.9.3b)
breadboards: 1

parts:
  R1 = Resistor [tolerance=±5% resistance=10k package=THT]
  Arduino1 = Arduino Uno (Rev3)
  BUTTON1 = Arcade Button (blue)
  LED1 = RGB LED - (4 legs) [package="5 mm [THT]"]
  Part1 = Adafruit TB6612 DC and Stepper Motor Driver [part_number="Adafruit #2448"]
  Part2 = Adafruit Audio FX Mini Sound Board [part_number="Adafruit #2342 and #2220"]
  Part3 = Mono 2.5W Class D Audio Amplifier - PAM8302
  SP1 = SPEAKER [package=pcb_mount_speaker]
  MOTOR1 = Adafruit Gear-Reduced Stepper Motor (small)

nets:
  N1: R1.Pin_0, Arduino1.D2, BUTTON1.no_name_yet#2
  GND: R1.Pin_1, Arduino1.GND, LED1.green_cathode, Part1.GND, Part2.GND, Part3.GND, Part3.AIN-, MOTOR1.RED
  N2: Arduino1.D8, Part1.AIN1
  N3: Arduino1.D9_PWM, Part1.BIN1
  N4: Arduino1.D10_PWM/SS, Part1.BIN2
  N5: Arduino1.D3_PWM, Part2.GPIO0_1
  N6: Arduino1.D4, Part2.GPIO0_0
  N7: Arduino1.D5_PWM, Part2.GPIO0_2
  N8: Arduino1.D6_PWM, LED1.red_cathode
  N9: Arduino1.D7, Part1.AIN2
  VCC: Arduino1.5V, BUTTON1.no_name_yet#1, LED1.common_anode, Part1.VCC, Part1.PWMB, Part1.PWMA, Part2.VIN, Part3.VCC
  N10: Arduino1.VIN, Part1.PWRIN
  N11: Part1.MOTORA1, MOTOR1.ORANGE
  N12: Part1.MOTORA2, MOTOR1.PINK
  N13: Part1.MOTORB2, MOTOR1.YELLOW
  N14: Part1.MOTORB1, MOTOR1.BLUE
  N15: Part2.R_AC, Part3.AIN+
  N16: Part3.VO+, SP1.+
  N17: Part3.VO-, SP1.-

custom parts:
  Arcade Button (blue): Adafruit Arcade Button (blue)
  Adafruit TB6612 DC and Stepper Motor Driver: Spin two DC motors, step one bi-polar or uni-polar stepper, or fire off two solenoids with 1.2A per channel using the TB6612. These are perhaps better known as "the drivers in our assembled Adafruit Motorshield or Motor HAT." We really like these dual H-bridges, so if you want to control motors without a shield or HAT these are easy to include on any solderless breadboard or perma-proto.
  Adafruit Audio FX Mini Sound Board: Would you like to add audio/sound effects to your next project, without an Arduino+Shield? Or maybe you don't even know how to use microcontrollers, you just want to make a sound play whenever you press a button. What about something that has to be very small and portable? You are probably feeling a little frustrated: it's been very hard to find a simple, low cost audio effects trigger that is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
  Mono 2.5W Class D Audio Amplifier - PAM8302: A super small but powerful mono amplifier able to deliver up to 2.5 Watts into 4-8 ohm impedance speakers. Inside the miniature chip is a class D controller, able to run from 2.0V-5.5VDC. Since the amp is a class D, its very efficient (over 90% efficient when driving an 8Ω speaker at over half a Watt) - making it perfect for portable and battery-powered projects.
  Adafruit Gear-Reduced Stepper Motor (small): Adafruit gear-reduction stepper motor (small)

// code stored in the sketch: Button.ino
/*
  Button
 
 Turns on and off a light emitting diode(LED) connected to digital  
 pin 13, when pressing a pushbutton attached to pin 2. 
 
 
 The circuit:
 * LED attached from pin 13 to ground 
 * pushbutton attached to pin 2 from +5V
 * 10K resistor attached to pin 2 from ground
 
 * Note: on most Arduinos there is already an LED on the board
 attached to pin 13.
 
 
 created 2005
 by DojoDave <http://www.0j0.org>
 modified 30 Aug 2011
 by Tom Igoe
 
 This example code is in the public domain.
 
 http://www.arduino.cc/en/Tutorial/Button
 */

// constants won't change. They're used here to 
// set pin numbers:
const int buttonPin = 2;     // the number of the pushbutton pin
const int ledPin =  13;      // the number of the LED pin

// variables will change:
int buttonState = 0;         // variable for reading the pushbutton status

void setup() {
  // initialize the LED pin as an output:
  pinMode(ledPin, OUTPUT);      
  // initialize the pushbutton pin as an input:
  pinMode(buttonPin, INPUT);     
}

void loop(){
  // read the state of the pushbutton value:
  buttonState = digitalRead(buttonPin);

  // check if the pushbutton is pressed.
  // if it is, the buttonState is HIGH:
  if (buttonState == HIGH) {     
    // turn LED on:    
    digitalWrite(ledPin, HIGH);  
  } 
  else {
    // turn LED off:
    digitalWrite(ledPin, LOW); 
  }
}
